# Fritzing sketch vibration_sensor_with_relay_and_external_5v_power_source_nikDyG3P0b (saved by Fritzing 0.9.3b)
breadboards: 1

parts:
  SW-420_Vibration_Sensor = Vibration sensor module
  BATT1 = 3xAAA Switchable Battery Pack w/JST connector
  Onderdeel1 = Arduino Uno (Rev3) - ICSP
  Relay = DS2Y-5-DC5V [part_number=DS2Y-5-DC5V]
  LED1 = LED - 3mm [color="Red (633nm)" package="3 mm [THT]"]
  LED2 = LED - 3mm [color="Red (633nm)" package="3 mm [THT]"]
  part = Resistor [tolerance=±5% resistance=220 package=THT]
  part_2 = Resistor [tolerance=±5% resistance=220 package=THT]
  PC817_Optocoupler = Sharp PC817 [package=THT]
  BC547_Transistor = NPN-Transistor [package="TO92 [THT]"]
  1N4007_Diode = Diode [package=diode-1n4001]  # not connected
  part_3 = Resistor [tolerance=±5% resistance=220 package=THT]

nets:
  VCC: SW-420_Vibration_Sensor.vcc, Onderdeel1.5V, PC817_Optocoupler.Pin_1
  N1: SW-420_Vibration_Sensor.Ground, Onderdeel1.GND
  N2: SW-420_Vibration_Sensor.Digital_output, Onderdeel1.D2
  N3: BATT1.POS, Relay.8_N.O., Relay.6_N.C., PC817_Optocoupler.Pin_4
  N4: BATT1.NEG, LED2.cathode, BC547_Transistor.B
  N5: Onderdeel1.D13/SCK, LED1.cathode
  N6: Relay.1_+, part_3.Pin_0
  N7: Relay.9_N.O., BC547_Transistor.E
  N8: LED1.anode, part_2.Pin_1
  N9: LED2.anode, part_3.Pin_1
  N10: part.Pin_0, PC817_Optocoupler.Pin_3
  N11: part.Pin_1, BC547_Transistor.C
  N12: part_2.Pin_0, PC817_Optocoupler.Pin_2

custom parts:
  Vibration sensor module: Single-roller type full induction trigger switch. When no vibration or tilt, the product is ON conduction state, and in the steady state, when a vibration or tilt, the switch will be rendered instantly disconnect the conductive resistance increases, generating a current pulse signal, thereby triggering circuit. The default state of the swith is close Digital output Supply voltage:3.3V-5V On-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
  3xAAA Switchable Battery Pack w/JST connector: 3xAAA Switchable Battery Pack with JST connector
